// Digital circuit FSM.dig as structural Verilog
module FSM (
  input  [3:0] op,
  input  clk
);

  wire dipswitch_1_out;
  wire [3:0] counter_1_out;
  wire [7:0] FSM_0_d, FSM_1_d, FSM_2_d;
  wire [11:8] interrupt_out;

  Counter #(.Bits(4)) counter_1 (.en(1'b1), .C(clk), .clr(dipswitch_1_out), .out(counter_1_out));  // open: ovf
  DipSwitch dipswitch_1 (.out(dipswitch_1_out));
  DipSwitch interrupt (.out(interrupt_out[8]));
  DipSwitch op2 (.out(interrupt_out[9]));
  DipSwitch jcmp (.out(interrupt_out[10]));
  DipSwitch reset (.out(interrupt_out[11]));
  EEPROM #(.AddrBits(12), .Bits(8)) FSM_0 (
    .A({interrupt_out, op, counter_1_out}), .CS(1'b1), .WE(1'b0), .OE(1'b1), .D(FSM_0_d));
  EEPROM #(.AddrBits(12), .Bits(8)) FSM_1 (
    .A({interrupt_out, op, counter_1_out}), .CS(1'b1), .WE(1'b0), .OE(1'b1), .D(FSM_1_d));
  EEPROM #(.AddrBits(12), .Bits(8)) FSM_2 (
    .A({interrupt_out, op, counter_1_out}), .CS(1'b1), .WE(1'b0), .OE(1'b1), .D(FSM_2_d));
  LED Edata (.in(FSM_0_d[1]));
  LED Epc (.in(FSM_0_d[3]));
  LED Edip (.in(FSM_0_d[5]));
  LED Cir (.in(FSM_0_d[7]));
  LED sel_1 (.in(FSM_1_d[1]));
  LED E_rx (.in(FSM_1_d[3]));
  LED Cr_all (.in(FSM_1_d[5]));
  LED C_p1 (.in(FSM_1_d[7]));
  LED pcinc (.in(FSM_2_d[1]));
  LED Ccmp (.in(FSM_2_d[3]));
  LED Cstack (.in(FSM_2_d[5]));
  LED csp (.in(FSM_2_d[7]));
  LED C_p0 (.in(FSM_0_d[0]));
  LED Cdata (.in(FSM_0_d[2]));
  LED Cpc (.in(FSM_0_d[4]));
  LED Cmar (.in(FSM_0_d[6]));
  LED csp_plus__plus (.in(FSM_1_d[0]));
  LED sel_0 (.in(FSM_1_d[2]));
  LED C_rx (.in(FSM_1_d[4]));
  LED Ealu (.in(FSM_1_d[6]));
  LED NULL (.in(FSM_2_d[0]));
  LED setsub (.in(FSM_2_d[2]));
  LED Estack (.in(FSM_2_d[4]));
  LED Einstr (.in(FSM_2_d[6]));

  // Notes on the sheet:
  //   contents of FSM_0 (hex, n*v repeats v):
  //   80,1,6*0,80,1,6*0,80,7*0,80,7*0,80,40,4,5*0,80,40,4,5*0,80,40
  //   ,2,5*0,80,40,2,5*0,80,1,6*0,80,1,6*0,80,1,6*0,80,1,6*0,80,1,6*0
  //   ,80,1,6*0,80,1,6*0,80,1,6*0,80,1,6*0,80,1,6*0,80,1,6*0,80,1,6*0
  //   ,80,1,6*0,80,1,6*0,80,1,6*0,80,1,6*0,80,7*0,80,7*0,80,7*0,80,7*0
  //   ,80,10,6*0,80,10,6*0,80,7*0,80,7*0,8,0,30,5*0,8,0,30,5*0,8,0,30
  //   ,5*0,8,0,30,5*0,8,0,30,5*0,8,0,30,5*0,8,0,30,5*0,8,0,30,5*0,8
  //   ,0,30,5*0,8,0,30,5*0,8,0,30,5*0,8,0,30,5*0,8,0,30,5*0,8,0,30,5*0
  //   ,8,0,30,5*0,8,0,30,5*0,8,0,30,5*0,8,0,30,5*0,8,0,30,5*0,8,0,30
  //   ,5*0,8,0,30,5*0,8,0,30,5*0,8,0,30,5*0,8,0,30,5*0,8,0,30,5*0,8
  //   ,0,30,5*0,8,0,30,5*0,8,0,30,5*0,8,0,30,5*0,8,0,30,5*0,8,0,30,5*0
  //   ,8,0,30,5*0,80,1,6*0,80,1,6*0,80,7*0,80,7*0,80,40,4,5*0,80,40
  //   ,4,5*0,80,40,2,5*0,80,40,2,5*0,80,1,6*0,80,1,6*0,80,1,6*0,80,1
  //   ,6*0,80,1,6*0,80,1,6*0,80,1,6*0,80,1,6*0,80,1,6*0,80,1,6*0,80
  //   ,1,6*0,80,1,6*0,80,1,6*0,80,1,6*0,80,1,6*0,80,1,6*0,80,8,6*0,80
  //   ,8,6*0,80,0,10,5*0,80,0,10,5*0,80,10,6*0,80,10,6*0,80,7*0,80,7*0
  //   ,8,0,30,5*0,8,0,30,5*0,8,0,30,5*0,8,0,30,5*0,8,0,30,5*0,8,0,30
  //   ,5*0,8,0,30,5*0,8,0,30,5*0,8,0,30,5*0,8,0,30,5*0,8,0,30,5*0,8
  //   ,0,30,5*0,8,0,30,5*0,8,0,30,5*0,8,0,30,5*0,8,0,30,5*0,8,0,30,5*0
  //   ,8,0,30,5*0,8,0,30,5*0,8,0,30,5*0,8,0,30,5*0,8,0,30,5*0,8,0,30
  //   ,5*0,8,0,30,5*0,8,0,30,5*0,8,0,30,5*0,8,0,30,5*0,8,0,30,5*0,8
  //   ,0,30,5*0,8,0,30,5*0,8,0,30,5*0,8,0,30,5*0,80,1,6*0,80,1,6*0,80
  //   ,7*0,80,7*0,80,40,4,5*0,80,40,4,5*0,80,40,2,5*0,80,40,2,5*0,80
  //   ,1,6*0,80,1,6*0,80,1,6*0,80,1,6*0,80,1,6*0,80,1,6*0,80,1,6*0,80
  //   ,1,6*0,80,1,6*0,80,1,6*0,80,1,6*0,80,1,6*0,80,1,6*0,80,1,6*0,80
  //   ,1,6*0,80,1,6*0,80,7*0,80,7*0,80,7*0,80,7*0,80,10,6*0,80,10,6*0
  //   ,80,0,10,5*0,80,0,10,5*0,8,0,30,5*0,8,0,30,5*0,8,0,30,5*0,8,0
  //   ,30,5*0,8,0,30,5*0,8,0,30,5*0,8,0,30,5*0,8,0,30,5*0,8,0,30,5*0
  //   ,8,0,30,5*0,8,0,30,5*0,8,0,30,5*0,8,0,30,5*0,8,0,30,5*0,8,0,30
  //   ,5*0,8,0,30,5*0,8,0,30,5*0,8,0,30,5*0,8,0,30,5*0,8,0,30,5*0,8
  //   ,0,30,5*0,8,0,30,5*0,8,0,30,5*0,8,0,30,5*0,8,0,30,5*0,8,0,30,5*0
  //   ,8,0,30,5*0,8,0,30,5*0,8,0,30,5*0,8,0,30,5*0,8,0,30,5*0,8,0,30
  //   ,5*0,80,1,6*0,80,1,6*0,80,7*0,80,7*0,80,40,4,5*0,80,40,4,5*0,80
  //   ,40,2,5*0,80,40,2,5*0,80,1,6*0,80,1,6*0,80,1,6*0,80,1,6*0,80,1
  //   ,6*0,80,1,6*0,80,1,6*0,80,1,6*0,80,1,6*0,80,1,6*0,80,1,6*0,80
  //   ,1,6*0,80,1,6*0,80,1,6*0,80,1,6*0,80,1,6*0,80,8,6*0,80,8,6*0,80
  //   ,0,10,5*0,80,0,10,5*0,80,10,6*0,80,10,6*0,80,0,10,5*0,80,0,10
  //   ,5*0,8,0,30,5*0,8,0,30,5*0,8,0,30,5*0,8,0,30,5*0,8,0,30,5*0,8
  //   ,0,30,5*0,8,0,30,5*0,8,0,30,5*0,8,0,30,5*0,8,0,30,5*0,8,0,30,5*0
  //   ,8,0,30,5*0,8,0,30,5*0,8,0,30,5*0,8,0,30,5*0,8,0,30,5*0,8,0,30
  //   ,5*0,8,0,30,5*0,8,0,30,5*0,8,0,30,5*0,8,0,30,5*0,8,0,30,5*0,8
  //   ,0,30,5*0,8,0,30,5*0,8,0,30,5*0,8,0,30,5*0,8,0,30,5*0,8,0,30,5*0
  //   ,8,0,30,5*0,8,0,30,5*0,8,0,30,5*0,8,0,30,5*0,d0,7*0,d0,7*0,d0
  //   ,7*0,d0,7*0,d0,7*0,d0,7*0,d0,7*0,d0,7*0,d0,7*0,d0,7*0,d0,7*0,d0
  //   ,7*0,d0,7*0,d0,7*0,d0,7*0,d0,7*0,d0,7*0,d0,7*0,d0,7*0,d0,7*0,d0
  //   ,7*0,d0,7*0,d0,7*0,d0,7*0,d0,7*0,d0,7*0,d0,7*0,d0,7*0,d0,7*0,d0
  //   ,7*0,d0,7*0,d0,7*0,d0,7*0,d0,7*0,d0,7*0,d0,7*0,d0,7*0,d0,7*0,d0
  //   ,7*0,d0,7*0,d0,7*0,d0,7*0,d0,7*0,d0,7*0,d0,7*0,d0,7*0,d0,7*0,d0
  //   ,7*0,d0,7*0,d0,7*0,d0,7*0,d0,7*0,d0,7*0,d0,7*0,d0,7*0,d0,7*0,d0
  //   ,7*0,d0,7*0,d0,7*0,d0,7*0,d0,7*0,d0,7*0,d0,7*0,d0,7*0,d0,7*0,d0
  //   ,7*0,d0,7*0,d0,7*0,d0,7*0,d0,7*0,d0,7*0,d0,7*0,d0,7*0,d0,7*0,d0
  //   ,7*0,d0,7*0,d0,7*0,d0,7*0,d0,7*0,d0,7*0,d0,7*0,d0,7*0,d0,7*0,d0
  //   ,7*0,d0,7*0,d0,7*0,d0,7*0,d0,7*0,d0,7*0,d0,7*0,d0,7*0,d0,7*0,d0
  //   ,7*0,d0,7*0,d0,7*0,d0,7*0,d0,7*0,d0,7*0,d0,7*0,d0,7*0,d0,7*0,d0
  //   ,7*0,d0,7*0,d0,7*0,d0,7*0,d0,7*0,d0,7*0,d0,7*0,d0,7*0,d0,7*0,d0
  //   ,7*0,d0,7*0,d0,7*0,d0,7*0,d0,7*0,d0,7*0,d0,7*0,d0,7*0,d0,7*0,d0
  //   ,7*0,d0,7*0,d0,7*0,d0,7*0,d0,7*0,d0,7*0,d0,7*0,d0,7*0,d0,7*0,d0
  //   ,7*0,d0,7*0,d0,7*0,d0,7*0,d0,7*0,d0,7*0,d0,7*0,d0,7*0,d0,7*0,d0
  //   ,7*0,d0,7*0,d0,7*0,d0,7*0,d0,7*0,d0,7*0,d0,7*0,d0,7*0,d0,7*0,d0
  //   ,7*0,d0,7*0,d0,7*0,d0,7*0,d0,7*0,d0,7*0,d0,7*0,d0,7*0,d0,7*0,d0
  //   ,7*0,d0,7*0,d0,7*0,d0,7*0,d0,7*0,d0,7*0,d0,7*0,d0,7*0,d0,7*0,d0
  //   ,7*0,d0,7*0,d0,7*0,d0,7*0,d0,7*0,d0,7*0,d0,7*0,d0,7*0,d0,7*0,d0
  //   ,7*0,d0,7*0,d0,7*0,d0,7*0,d0,7*0,d0,7*0,d0,7*0,d0,7*0,d0,7*0,d0
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  //   contents of FSM_1 (hex, n*v repeats v):
  //   0,8,52,6*0,8,52,7*0,12,7*0,12,6*0,c,8,6*0,c,8,6*0,8,12,6*0,8,12
  //   ,6*0,8,8c,52,5*0,8,8c,52,5*0,8,52,6*0,8,52,6*0,8,8c,52,5*0,8,8c
  //   ,52,5*0,8,8c,52,5*0,8,8c,52,5*0,8,8c,52,5*0,8,8c,52,5*0,8,8c,52
  //   ,5*0,8,8c,52,5*0,8,52,6*0,8,52,6*0,8,52,6*0,8,52,6*0,8,1,6*0,8
  //   ,1,7*0,12,7*0,12,6*0,8,7*0,8,7*0,c,7*0,c,7*0,1,7*0,1,7*0,1,7*0
  //   ,1,7*0,1,7*0,1,7*0,1,7*0,1,7*0,1,7*0,1,7*0,1,7*0,1,7*0,1,7*0,1
  //   ,7*0,1,7*0,1,7*0,1,7*0,1,7*0,1,7*0,1,7*0,1,7*0,1,7*0,1,7*0,1,7*0
  //   ,1,7*0,1,7*0,1,7*0,1,7*0,1,7*0,1,7*0,1,7*0,1,7*0,8,52,6*0,8,52
  //   ,7*0,12,7*0,12,6*0,c,8,6*0,c,8,6*0,8,12,6*0,8,12,6*0,8,8c,52,5*0
  //   ,8,8c,52,5*0,8,52,6*0,8,52,6*0,8,8c,52,5*0,8,8c,52,5*0,8,8c,52
  //   ,5*0,8,8c,52,5*0,8,8c,52,5*0,8,8c,52,5*0,8,8c,52,5*0,8,8c,52,5*0
  //   ,8,52,6*0,8,52,6*0,8,52,6*0,8,52,7*0,1,7*0,1,22*0,8,7*0,8,7*0
  //   ,c,7*0,c,7*0,1,7*0,1,7*0,1,7*0,1,7*0,1,7*0,1,7*0,1,7*0,1,7*0,1
  //   ,7*0,1,7*0,1,7*0,1,7*0,1,7*0,1,7*0,1,7*0,1,7*0,1,7*0,1,7*0,1,7*0
  //   ,1,7*0,1,7*0,1,7*0,1,7*0,1,7*0,1,7*0,1,7*0,1,7*0,1,7*0,1,7*0,1
  //   ,7*0,1,7*0,1,7*0,8,52,6*0,8,52,7*0,12,7*0,12,6*0,c,8,6*0,c,8,6*0
  //   ,8,12,6*0,8,12,6*0,8,8c,52,5*0,8,8c,52,5*0,8,52,6*0,8,52,6*0,8
  //   ,8c,52,5*0,8,8c,52,5*0,8,8c,52,5*0,8,8c,52,5*0,8,8c,52,5*0,8,8c
  //   ,52,5*0,8,8c,52,5*0,8,8c,52,5*0,8,52,6*0,8,52,6*0,8,52,6*0,8,52
  //   ,6*0,8,1,6*0,8,1,7*0,12,7*0,12,6*0,8,7*0,8,7*0,c,8,6*0,c,8,6*0
  //   ,1,7*0,1,7*0,1,7*0,1,7*0,1,7*0,1,7*0,1,7*0,1,7*0,1,7*0,1,7*0,1
  //   ,7*0,1,7*0,1,7*0,1,7*0,1,7*0,1,7*0,1,7*0,1,7*0,1,7*0,1,7*0,1,7*0
  //   ,1,7*0,1,7*0,1,7*0,1,7*0,1,7*0,1,7*0,1,7*0,1,7*0,1,7*0,1,7*0,1
  //   ,7*0,8,52,6*0,8,52,7*0,12,7*0,12,6*0,c,8,6*0,c,8,6*0,8,12,6*0
  //   ,8,12,6*0,8,8c,52,5*0,8,8c,52,5*0,8,52,6*0,8,52,6*0,8,8c,52,5*0
  //   ,8,8c,52,5*0,8,8c,52,5*0,8,8c,52,5*0,8,8c,52,5*0,8,8c,52,5*0,8
  //   ,8c,52,5*0,8,8c,52,5*0,8,52,6*0,8,52,6*0,8,52,6*0,8,52,7*0,1,7*0
  //   ,1,22*0,8,7*0,8,7*0,c,8,6*0,c,8,6*0,1,7*0,1,7*0,1,7*0,1,7*0,1
  //   ,7*0,1,7*0,1,7*0,1,7*0,1,7*0,1,7*0,1,7*0,1,7*0,1,7*0,1,7*0,1,7*0
  //   ,1,7*0,1,7*0,1,7*0,1,7*0,1,7*0,1,7*0,1,7*0,1,7*0,1,7*0,1,7*0,1
  //   ,7*0,1,7*0,1,7*0,1,7*0,1,7*0,1,7*0,1,6*0,20,7*0,20,7*0,20,7*0
  //   ,20,7*0,20,7*0,20,7*0,20,7*0,20,7*0,20,7*0,20,7*0,20,7*0,20,7*0
  //   ,20,7*0,20,7*0,20,7*0,20,7*0,20,7*0,20,7*0,20,7*0,20,7*0,20,7*0
  //   ,20,7*0,20,7*0,20,7*0,20,7*0,20,7*0,20,7*0,20,7*0,20,7*0,20,7*0
  //   ,20,7*0,20,7*0,20,7*0,20,7*0,20,7*0,20,7*0,20,7*0,20,7*0,20,7*0
  //   ,20,7*0,20,7*0,20,7*0,20,7*0,20,7*0,20,7*0,20,7*0,20,7*0,20,7*0
  //   ,20,7*0,20,7*0,20,7*0,20,7*0,20,7*0,20,7*0,20,7*0,20,7*0,20,7*0
  //   ,20,7*0,20,7*0,20,7*0,20,7*0,20,7*0,20,7*0,20,7*0,20,7*0,20,7*0
  //   ,20,7*0,20,7*0,20,7*0,20,7*0,20,7*0,20,7*0,20,7*0,20,7*0,20,7*0
  //   ,20,7*0,20,7*0,20,7*0,20,7*0,20,7*0,20,7*0,20,7*0,20,7*0,20,7*0
  //   ,20,7*0,20,7*0,20,7*0,20,7*0,20,7*0,20,7*0,20,7*0,20,7*0,20,7*0
  //   ,20,7*0,20,7*0,20,7*0,20,7*0,20,7*0,20,7*0,20,7*0,20,7*0,20,7*0
  //   ,20,7*0,20,7*0,20,7*0,20,7*0,20,7*0,20,7*0,20,7*0,20,7*0,20,7*0
  //   ,20,7*0,20,7*0,20,7*0,20,7*0,20,7*0,20,7*0,20,7*0,20,7*0,20,7*0
  //   ,20,7*0,20,7*0,20,7*0,20,7*0,20,7*0,20,7*0,20,7*0,20,7*0,20,7*0
  //   ,20,7*0,20,7*0,20,7*0,20,7*0,20,7*0,20,7*0,20,7*0,20,7*0,20,7*0
  //   ,20,7*0,20,7*0,20,7*0,20,7*0,20,7*0,20,7*0,20,7*0,20,7*0,20,7*0
  //   ,20,7*0,20,7*0,20,7*0,20,7*0,20,7*0,20,7*0,20,7*0,20,7*0,20,7*0
  //   ,20,7*0,20,7*0,20,7*0,20,7*0,20,7*0,20,7*0,20,7*0,20,7*0,20,7*0
  //   ,20,7*0,20,7*0,20,7*0,20,7*0,20,7*0,20,7*0,20,7*0,20,7*0,20,7*0
  //   ,20,7*0,20,7*0,20,7*0,20,7*0,20,7*0,20,7*0,20,7*0,20,7*0,20,7*0
  //   ,20,7*0,20,7*0,20,7*0,20,7*0,20,7*0,20,7*0,20,7*0,20,7*0,20,7*0
  //   ,20,7*0,20,7*0,20,7*0,20,7*0,20,7*0,20,7*0,20,7*0,20,7*0,20,7*0
  //   ,20,7*0,20,7*0,20,7*0,20,7*0,20,7*0,20,7*0,20,7*0,20,7*0,20,7*0
  //   ,20,7*0,20,7*0,20,7*0,20,7*0,20,7*0,20,7*0,20,7*0,20,7*0,20,7*0
  //   ,20,7*0,20,7*0,20,7*0,20,7*0,20,7*0,20,7*0,20,7*0,20,7*0,20,7*0
  //   ,20,7*0,20,7*0,20,7*0,20,7*0,20,7*0,20,7*0,20,7*0,20,7*0,20,7*0
  //   ,20,7*0,20,7*0,20,7*0,20,7*0,20,7*0,20,7*0,20,7*0,20,7*0,20,7*0
  //   ,20,7*0,20,7*0,20,7*0,20,7*0,20,7*0,20,7*0,20,7*0,20,7*0,20,7*0,20
  //   contents of FSM_2 (hex, n*v repeats v):
  //   40,0,0,6,4*0,40,0,0,6,4*0,40,2,40,6,4*0,40,2,40,6,4*0,40,0,0,6
  //   ,4*0,40,0,0,6,4*0,40,0,0,6,4*0,40,0,0,6,4*0,40,0,0,0,6,0,0,0,40
  //   ,0,0,0,6,0,0,0,40,0,0,6,4*0,40,0,0,6,4*0,40,0,0,0,6,0,0,0,40,0,0,0
  //   ,6,0,0,0,40,0,0,0,6,0,0,0,40,0,0,0,6,0,0,0,40,0,0,0,6,0,0,0,40
  //   ,0,0,0,6,0,0,0,40,0,0,0,6,0,0,0,40,0,0,0,6,0,0,0,40,0,0,6,4*0
  //   ,40,0,0,6,4*0,40,0,0,6,4*0,40,0,0,6,4*0,40,20,0,6,4*0,40,20,0
  //   ,6,4*0,40,80,10,6,4*0,40,80,10,6,4*0,40,0,4,5*0,40,0,4,5*0,40
  //   ,8,6,5*0,40,8,6,5*0,20,0,0,4,4*0,20,0,0,4,4*0,20,0,0,4,4*0,20
  //   ,0,0,4,4*0,20,0,0,4,4*0,20,0,0,4,4*0,20,0,0,4,4*0,20,0,0,4,4*0
  //   ,20,0,0,4,4*0,20,0,0,4,4*0,20,0,0,4,4*0,20,0,0,4,4*0,20,0,0,4
  //   ,4*0,20,0,0,4,4*0,20,0,0,4,4*0,20,0,0,4,4*0,20,0,0,4,4*0,20,0,0
  //   ,4,4*0,20,0,0,4,4*0,20,0,0,4,4*0,20,0,0,4,4*0,20,0,0,4,4*0,20
  //   ,0,0,4,4*0,20,0,0,4,4*0,20,0,0,4,4*0,20,0,0,4,4*0,20,0,0,4,4*0
  //   ,20,0,0,4,4*0,20,0,0,4,4*0,20,0,0,4,4*0,20,0,0,4,4*0,20,0,0,4
  //   ,4*0,40,0,0,6,4*0,40,0,0,6,4*0,40,2,40,6,4*0,40,2,40,6,4*0,40
  //   ,0,0,6,4*0,40,0,0,6,4*0,40,0,0,6,4*0,40,0,0,6,4*0,40,0,0,0,6,0,0,0
  //   ,40,0,0,0,6,0,0,0,40,0,0,6,4*0,40,0,0,6,4*0,40,0,0,0,6,0,0,0,40
  //   ,0,0,0,6,0,0,0,40,0,0,0,6,0,0,0,40,0,0,0,6,0,0,0,40,0,0,0,6,0,0,0
  //   ,40,0,0,0,6,0,0,0,40,0,0,0,6,0,0,0,40,0,0,0,6,0,0,0,40,0,0,6,4*0
  //   ,40,0,0,6,4*0,40,0,0,6,4*0,40,0,0,6,4*0,40,20,0,6,4*0,40,20,0
  //   ,6,4*0,40,80,10,4,4*0,40,80,10,4,4*0,40,0,4,5*0,40,0,4,5*0,40
  //   ,8,6,5*0,40,8,6,5*0,20,0,0,4,4*0,20,0,0,4,4*0,20,0,0,4,4*0,20
  //   ,0,0,4,4*0,20,0,0,4,4*0,20,0,0,4,4*0,20,0,0,4,4*0,20,0,0,4,4*0
  //   ,20,0,0,4,4*0,20,0,0,4,4*0,20,0,0,4,4*0,20,0,0,4,4*0,20,0,0,4
  //   ,4*0,20,0,0,4,4*0,20,0,0,4,4*0,20,0,0,4,4*0,20,0,0,4,4*0,20,0,0
  //   ,4,4*0,20,0,0,4,4*0,20,0,0,4,4*0,20,0,0,4,4*0,20,0,0,4,4*0,20
  //   ,0,0,4,4*0,20,0,0,4,4*0,20,0,0,4,4*0,20,0,0,4,4*0,20,0,0,4,4*0
  //   ,20,0,0,4,4*0,20,0,0,4,4*0,20,0,0,4,4*0,20,0,0,4,4*0,20,0,0,4
  //   ,4*0,40,0,0,6,4*0,40,0,0,6,4*0,40,2,40,6,4*0,40,2,40,6,4*0,40
  //   ,0,0,6,4*0,40,0,0,6,4*0,40,0,0,6,4*0,40,0,0,6,4*0,40,0,0,0,6,0,0,0
  //   ,40,0,0,0,6,0,0,0,40,0,0,6,4*0,40,0,0,6,4*0,40,0,0,0,6,0,0,0,40
  //   ,0,0,0,6,0,0,0,40,0,0,0,6,0,0,0,40,0,0,0,6,0,0,0,40,0,0,0,6,0,0,0
  //   ,40,0,0,0,6,0,0,0,40,0,0,0,6,0,0,0,40,0,0,0,6,0,0,0,40,0,0,6,4*0
  //   ,40,0,0,6,4*0,40,0,0,6,4*0,40,0,0,6,4*0,40,20,0,6,4*0,40,20,0
  //   ,6,4*0,40,80,10,6,4*0,40,80,10,6,4*0,40,0,4,5*0,40,0,4,5*0,40
  //   ,8,0,4,4*0,40,8,0,4,4*0,20,0,0,4,4*0,20,0,0,4,4*0,20,0,0,4,4*0
  //   ,20,0,0,4,4*0,20,0,0,4,4*0,20,0,0,4,4*0,20,0,0,4,4*0,20,0,0,4
  //   ,4*0,20,0,0,4,4*0,20,0,0,4,4*0,20,0,0,4,4*0,20,0,0,4,4*0,20,0,0
  //   ,4,4*0,20,0,0,4,4*0,20,0,0,4,4*0,20,0,0,4,4*0,20,0,0,4,4*0,20
  //   ,0,0,4,4*0,20,0,0,4,4*0,20,0,0,4,4*0,20,0,0,4,4*0,20,0,0,4,4*0
  //   ,20,0,0,4,4*0,20,0,0,4,4*0,20,0,0,4,4*0,20,0,0,4,4*0,20,0,0,4
  //   ,4*0,20,0,0,4,4*0,20,0,0,4,4*0,20,0,0,4,4*0,20,0,0,4,4*0,20,0,0
  //   ,4,4*0,40,0,0,6,4*0,40,0,0,6,4*0,40,2,40,6,4*0,40,2,40,6,4*0,40
  //   ,0,0,6,4*0,40,0,0,6,4*0,40,0,0,6,4*0,40,0,0,6,4*0,40,0,0,0,6,0,0,0
  //   ,40,0,0,0,6,0,0,0,40,0,0,6,4*0,40,0,0,6,4*0,40,0,0,0,6,0,0,0,40
  //   ,0,0,0,6,0,0,0,40,0,0,0,6,0,0,0,40,0,0,0,6,0,0,0,40,0,0,0,6,0,0,0
  //   ,40,0,0,0,6,0,0,0,40,0,0,0,6,0,0,0,40,0,0,0,6,0,0,0,40,0,0,6,4*0
  //   ,40,0,0,6,4*0,40,0,0,6,4*0,40,0,0,6,4*0,40,20,0,6,4*0,40,20,0
  //   ,6,4*0,40,80,10,4,4*0,40,80,10,4,4*0,40,0,4,5*0,40,0,4,5*0,40
  //   ,8,0,4,4*0,40,8,0,4,4*0,20,0,0,4,4*0,20,0,0,4,4*0,20,0,0,4,4*0
  //   ,20,0,0,4,4*0,20,0,0,4,4*0,20,0,0,4,4*0,20,0,0,4,4*0,20,0,0,4
  //   ,4*0,20,0,0,4,4*0,20,0,0,4,4*0,20,0,0,4,4*0,20,0,0,4,4*0,20,0,0
  //   ,4,4*0,20,0,0,4,4*0,20,0,0,4,4*0,20,0,0,4,4*0,20,0,0,4,4*0,20
  //   ,0,0,4,4*0,20,0,0,4,4*0,20,0,0,4,4*0,20,0,0,4,4*0,20,0,0,4,4*0
  //   ,20,0,0,4,4*0,20,0,0,4,4*0,20,0,0,4,4*0,20,0,0,4,4*0,20,0,0,4
  //   ,4*0,20,0,0,4,4*0,20,0,0,4,4*0,20,0,0,4,4*0,20,0,0,4,4*0,20,0,0
  //   ,4,5*0,4,7*0,4,7*0,4,7*0,4,7*0,4,7*0,4,7*0,4,7*0,4,7*0,4,7*0,4
  //   ,7*0,4,7*0,4,7*0,4,7*0,4,7*0,4,7*0,4,7*0,4,7*0,4,7*0,4,7*0,4,7*0
  //   ,4,7*0,4,7*0,4,7*0,4,7*0,4,7*0,4,7*0,4,7*0,4,7*0,4,7*0,4,7*0,4
  //   ,7*0,4,7*0,4,7*0,4,7*0,4,7*0,4,7*0,4,7*0,4,7*0,4,7*0,4,7*0,4,7*0
  //   ,4,7*0,4,7*0,4,7*0,4,7*0,4,7*0,4,7*0,4,7*0,4,7*0,4,7*0,4,7*0,4
  //   ,7*0,4,7*0,4,7*0,4,7*0,4,7*0,4,7*0,4,7*0,4,7*0,4,7*0,4,7*0,4,7*0
  //   ,4,7*0,4,7*0,4,7*0,4,7*0,4,7*0,4,7*0,4,7*0,4,7*0,4,7*0,4,7*0,4
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endmodule
