// Digital circuit RGBMatrix.dig as structural Verilog
module RGBMatrix (
  input  [11:0] Addr,
  input  [15:0] Data,
  input  CLK,
  output R1,
  output R2,
  output G1,
  output G2,
  output B1,
  output B2,
  output A,
  output B,
  output C,
  output D,
  output E,
  output LAT,
  output OE
);

  wire STRHI, STRLO;
  wire [2:0] U1_d2_2, U3_d2_2;
  wire [4:0] CTR_out_2, U1_d2, U3_d2;
  wire [5:0] CTR_out;
  wire [6:0] U2_d2, U4_d2;
  wire [7:2] E1_d, E2_d, E3_d;
  wire [7:7] U2_d2_2, U4_d2_2;

  Counter #(.Bits(16)) CTR (.en(1'b1), .C(CLK), .clr(1'b0), .out({CTR_out_2, E, D, C, B, A, CTR_out}));  // open: ovf
  Demultiplexer demultiplexer_1 (.sel(Addr[11]), .in(Data[15]), .out_0(STRLO), .out_1(STRHI));
  and and_1 (LAT, CTR_out[0], CTR_out[1], CTR_out[2], CTR_out[3], CTR_out[4], CTR_out[5]);
  RAMDualAccess #(.AddrBits(11), .Bits(8)) U1 (
    .str(STRLO), .C(CLK), .ld(1'b1), .A1(Addr[10:0]), .Din1(Data[7:0]), .A2({E, D, C, B, A, CTR_out}),
    .D2({U1_d2_2, U1_d2}));  // open: D1
  RAMDualAccess #(.AddrBits(11), .Bits(8)) U2 (
    .str(STRLO), .C(CLK), .ld(1'b1), .A1(Addr[10:0]), .Din1({1'b0, Data[14:8]}),
    .A2({E, D, C, B, A, CTR_out}), .D2({U2_d2_2[7], U2_d2}));  // open: D1
  RAMDualAccess #(.AddrBits(11), .Bits(8)) U3 (
    .str(STRHI), .C(CLK), .ld(1'b1), .A1(Addr[10:0]), .Din1(Data[7:0]), .A2({E, D, C, B, A, CTR_out}),
    .D2({U3_d2_2, U3_d2}));  // open: D1
  RAMDualAccess #(.AddrBits(11), .Bits(8)) U4 (
    .str(STRHI), .C(CLK), .ld(1'b1), .A1(Addr[10:0]), .Din1({1'b0, Data[14:8]}),
    .A2({E, D, C, B, A, CTR_out}), .D2({U4_d2_2[7], U4_d2}));  // open: D1
  EEPROM #(.AddrBits(15), .Bits(8)) E1 (
    .A({CTR_out_2, U3_d2, U1_d2}), .CS(1'b1), .WE(1'b0), .OE(1'b1), .D({E1_d, R2, R1}));
  EEPROM #(.AddrBits(15), .Bits(8)) E2 (
    .A({CTR_out_2, U4_d2[1:0], U3_d2_2, U2_d2[1:0], U1_d2_2}), .CS(1'b1), .WE(1'b0), .OE(1'b1),
    .D({E2_d, G2, G1}));
  EEPROM #(.AddrBits(15), .Bits(8)) E3 (
    .A({CTR_out_2, U4_d2[6:2], U2_d2[6:2]}), .CS(1'b1), .WE(1'b0), .OE(1'b1), .D({E3_d, B2, B1}));

  assign OE = LAT;

  // Other names for the same wires on the sheet: ADDRIN[10:0] = Addr[10:0]

  // Notes on the sheet:
  //   CLK: Hz: 2147483647
  //   contents of E1 (hex, n*v repeats v):
  //   0,31*1,2,31*3,2,31*3,2,31*3,2,31*3,2,31*3,2,31*3,2,31*3,2,31*3
  //   ,2,31*3,2,31*3,2,31*3,2,31*3,2,31*3,2,31*3,2,31*3,2,31*3,2,31*3
  //   ,2,31*3,2,31*3,2,31*3,2,31*3,2,31*3,2,31*3,2,31*3,2,31*3,2,31*3
  //   ,2,31*3,2,31*3,2,31*3,2,31*3,2,31*3,0,0,30*1,0,0,30*1,2,2,30*3
  //   ,2,2,30*3,2,2,30*3,2,2,30*3,2,2,30*3,2,2,30*3,2,2,30*3,2,2,30*3
  //   ,2,2,30*3,2,2,30*3,2,2,30*3,2,2,30*3,2,2,30*3,2,2,30*3,2,2,30*3
  //   ,2,2,30*3,2,2,30*3,2,2,30*3,2,2,30*3,2,2,30*3,2,2,30*3,2,2,30*3
  //   ,2,2,30*3,2,2,30*3,2,2,30*3,2,2,30*3,2,2,30*3,2,2,30*3,2,2,30*3
  //   ,2,2,30*3,0,0,0,29*1,0,0,0,29*1,0,0,0,29*1,2,2,2,29*3,2,2,2,29*3
  //   ,2,2,2,29*3,2,2,2,29*3,2,2,2,29*3,2,2,2,29*3,2,2,2,29*3,2,2,2
  //   ,29*3,2,2,2,29*3,2,2,2,29*3,2,2,2,29*3,2,2,2,29*3,2,2,2,29*3,2,2,2
  //   ,29*3,2,2,2,29*3,2,2,2,29*3,2,2,2,29*3,2,2,2,29*3,2,2,2,29*3,2,2,2
  //   ,29*3,2,2,2,29*3,2,2,2,29*3,2,2,2,29*3,2,2,2,29*3,2,2,2,29*3,2,2,2
  //   ,29*3,2,2,2,29*3,2,2,2,29*3,2,2,2,29*3,4*0,28*1,4*0,28*1,4*0,28*1
  //   ,4*0,28*1,4*2,28*3,4*2,28*3,4*2,28*3,4*2,28*3,4*2,28*3,4*2,28*3
  //   ,4*2,28*3,4*2,28*3,4*2,28*3,4*2,28*3,4*2,28*3,4*2,28*3,4*2,28*3
  //   ,4*2,28*3,4*2,28*3,4*2,28*3,4*2,28*3,4*2,28*3,4*2,28*3,4*2,28*3
  //   ,4*2,28*3,4*2,28*3,4*2,28*3,4*2,28*3,4*2,28*3,4*2,28*3,4*2,28*3
  //   ,4*2,28*3,5*0,27*1,5*0,27*1,5*0,27*1,5*0,27*1,5*0,27*1,5*2,27*3
  //   ,5*2,27*3,5*2,27*3,5*2,27*3,5*2,27*3,5*2,27*3,5*2,27*3,5*2,27*3
  //   ,5*2,27*3,5*2,27*3,5*2,27*3,5*2,27*3,5*2,27*3,5*2,27*3,5*2,27*3
  //   ,5*2,27*3,5*2,27*3,5*2,27*3,5*2,27*3,5*2,27*3,5*2,27*3,5*2,27*3
  //   ,5*2,27*3,5*2,27*3,5*2,27*3,5*2,27*3,5*2,27*3,6*0,26*1,6*0,26*1
  //   ,6*0,26*1,6*0,26*1,6*0,26*1,6*0,26*1,6*2,26*3,6*2,26*3,6*2,26*3
  //   ,6*2,26*3,6*2,26*3,6*2,26*3,6*2,26*3,6*2,26*3,6*2,26*3,6*2,26*3
  //   ,6*2,26*3,6*2,26*3,6*2,26*3,6*2,26*3,6*2,26*3,6*2,26*3,6*2,26*3
  //   ,6*2,26*3,6*2,26*3,6*2,26*3,6*2,26*3,6*2,26*3,6*2,26*3,6*2,26*3
  //   ,6*2,26*3,6*2,26*3,7*0,25*1,7*0,25*1,7*0,25*1,7*0,25*1,7*0,25*1
  //   ,7*0,25*1,7*0,25*1,7*2,25*3,7*2,25*3,7*2,25*3,7*2,25*3,7*2,25*3
  //   ,7*2,25*3,7*2,25*3,7*2,25*3,7*2,25*3,7*2,25*3,7*2,25*3,7*2,25*3
  //   ,7*2,25*3,7*2,25*3,7*2,25*3,7*2,25*3,7*2,25*3,7*2,25*3,7*2,25*3
  //   ,7*2,25*3,7*2,25*3,7*2,25*3,7*2,25*3,7*2,25*3,7*2,25*3,8*0,24*1
  //   ,8*0,24*1,8*0,24*1,8*0,24*1,8*0,24*1,8*0,24*1,8*0,24*1,8*0,24*1
  //   ,8*2,24*3,8*2,24*3,8*2,24*3,8*2,24*3,8*2,24*3,8*2,24*3,8*2,24*3
  //   ,8*2,24*3,8*2,24*3,8*2,24*3,8*2,24*3,8*2,24*3,8*2,24*3,8*2,24*3
  //   ,8*2,24*3,8*2,24*3,8*2,24*3,8*2,24*3,8*2,24*3,8*2,24*3,8*2,24*3
  //   ,8*2,24*3,8*2,24*3,8*2,24*3,9*0,23*1,9*0,23*1,9*0,23*1,9*0,23*1
  //   ,9*0,23*1,9*0,23*1,9*0,23*1,9*0,23*1,9*0,23*1,9*2,23*3,9*2,23*3
  //   ,9*2,23*3,9*2,23*3,9*2,23*3,9*2,23*3,9*2,23*3,9*2,23*3,9*2,23*3
  //   ,9*2,23*3,9*2,23*3,9*2,23*3,9*2,23*3,9*2,23*3,9*2,23*3,9*2,23*3
  //   ,9*2,23*3,9*2,23*3,9*2,23*3,9*2,23*3,9*2,23*3,9*2,23*3,9*2,23*3
  //   ,10*0,22*1,10*0,22*1,10*0,22*1,10*0,22*1,10*0,22*1,10*0,22*1,10*0
  //   ,22*1,10*0,22*1,10*0,22*1,10*0,22*1,10*2,22*3,10*2,22*3,10*2,22*3
  //   ,10*2,22*3,10*2,22*3,10*2,22*3,10*2,22*3,10*2,22*3,10*2,22*3,10*2
  //   ,22*3,10*2,22*3,10*2,22*3,10*2,22*3,10*2,22*3,10*2,22*3,10*2,22*3
  //   ,10*2,22*3,10*2,22*3,10*2,22*3,10*2,22*3,10*2,22*3,10*2,22*3,11*0
  //   ,21*1,11*0,21*1,11*0,21*1,11*0,21*1,11*0,21*1,11*0,21*1,11*0,21*1
  //   ,11*0,21*1,11*0,21*1,11*0,21*1,11*0,21*1,11*2,21*3,11*2,21*3,11*2
  //   ,21*3,11*2,21*3,11*2,21*3,11*2,21*3,11*2,21*3,11*2,21*3,11*2,21*3
  //   ,11*2,21*3,11*2,21*3,11*2,21*3,11*2,21*3,11*2,21*3,11*2,21*3,11*2
  //   ,21*3,11*2,21*3,11*2,21*3,11*2,21*3,11*2,21*3,11*2,21*3,12*0,20*1
  //   ,12*0,20*1,12*0,20*1,12*0,20*1,12*0,20*1,12*0,20*1,12*0,20*1,12*0
  //   ,20*1,12*0,20*1,12*0,20*1,12*0,20*1,12*0,20*1,12*2,20*3,12*2,20*3
  //   ,12*2,20*3,12*2,20*3,12*2,20*3,12*2,20*3,12*2,20*3,12*2,20*3,12*2
  //   ,20*3,12*2,20*3,12*2,20*3,12*2,20*3,12*2,20*3,12*2,20*3,12*2,20*3
  //   ,12*2,20*3,12*2,20*3,12*2,20*3,12*2,20*3,12*2,20*3,13*0,19*1,13*0
  //   ,19*1,13*0,19*1,13*0,19*1,13*0,19*1,13*0,19*1,13*0,19*1,13*0,19*1
  //   ,13*0,19*1,13*0,19*1,13*0,19*1,13*0,19*1,13*0,19*1,13*2,19*3,13*2
  //   ,19*3,13*2,19*3,13*2,19*3,13*2,19*3,13*2,19*3,13*2,19*3,13*2,19*3
  //   ,13*2,19*3,13*2,19*3,13*2,19*3,13*2,19*3,13*2,19*3,13*2,19*3,13*2
  //   ,19*3,13*2,19*3,13*2,19*3,13*2,19*3,13*2,19*3,14*0,18*1,14*0,18*1
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  //   contents of E2 (hex, n*v repeats v):
  //   0,31*1,2,31*3,2,31*3,2,31*3,2,31*3,2,31*3,2,31*3,2,31*3,2,31*3
  //   ,2,31*3,2,31*3,2,31*3,2,31*3,2,31*3,2,31*3,2,31*3,2,31*3,2,31*3
  //   ,2,31*3,2,31*3,2,31*3,2,31*3,2,31*3,2,31*3,2,31*3,2,31*3,2,31*3
  //   ,2,31*3,2,31*3,2,31*3,2,31*3,2,31*3,0,0,30*1,0,0,30*1,2,2,30*3
  //   ,2,2,30*3,2,2,30*3,2,2,30*3,2,2,30*3,2,2,30*3,2,2,30*3,2,2,30*3
  //   ,2,2,30*3,2,2,30*3,2,2,30*3,2,2,30*3,2,2,30*3,2,2,30*3,2,2,30*3
  //   ,2,2,30*3,2,2,30*3,2,2,30*3,2,2,30*3,2,2,30*3,2,2,30*3,2,2,30*3
  //   ,2,2,30*3,2,2,30*3,2,2,30*3,2,2,30*3,2,2,30*3,2,2,30*3,2,2,30*3
  //   ,2,2,30*3,0,0,0,29*1,0,0,0,29*1,0,0,0,29*1,2,2,2,29*3,2,2,2,29*3
  //   ,2,2,2,29*3,2,2,2,29*3,2,2,2,29*3,2,2,2,29*3,2,2,2,29*3,2,2,2
  //   ,29*3,2,2,2,29*3,2,2,2,29*3,2,2,2,29*3,2,2,2,29*3,2,2,2,29*3,2,2,2
  //   ,29*3,2,2,2,29*3,2,2,2,29*3,2,2,2,29*3,2,2,2,29*3,2,2,2,29*3,2,2,2
  //   ,29*3,2,2,2,29*3,2,2,2,29*3,2,2,2,29*3,2,2,2,29*3,2,2,2,29*3,2,2,2
  //   ,29*3,2,2,2,29*3,2,2,2,29*3,2,2,2,29*3,4*0,28*1,4*0,28*1,4*0,28*1
  //   ,4*0,28*1,4*2,28*3,4*2,28*3,4*2,28*3,4*2,28*3,4*2,28*3,4*2,28*3
  //   ,4*2,28*3,4*2,28*3,4*2,28*3,4*2,28*3,4*2,28*3,4*2,28*3,4*2,28*3
  //   ,4*2,28*3,4*2,28*3,4*2,28*3,4*2,28*3,4*2,28*3,4*2,28*3,4*2,28*3
  //   ,4*2,28*3,4*2,28*3,4*2,28*3,4*2,28*3,4*2,28*3,4*2,28*3,4*2,28*3
  //   ,4*2,28*3,5*0,27*1,5*0,27*1,5*0,27*1,5*0,27*1,5*0,27*1,5*2,27*3
  //   ,5*2,27*3,5*2,27*3,5*2,27*3,5*2,27*3,5*2,27*3,5*2,27*3,5*2,27*3
  //   ,5*2,27*3,5*2,27*3,5*2,27*3,5*2,27*3,5*2,27*3,5*2,27*3,5*2,27*3
  //   ,5*2,27*3,5*2,27*3,5*2,27*3,5*2,27*3,5*2,27*3,5*2,27*3,5*2,27*3
  //   ,5*2,27*3,5*2,27*3,5*2,27*3,5*2,27*3,5*2,27*3,6*0,26*1,6*0,26*1
  //   ,6*0,26*1,6*0,26*1,6*0,26*1,6*0,26*1,6*2,26*3,6*2,26*3,6*2,26*3
  //   ,6*2,26*3,6*2,26*3,6*2,26*3,6*2,26*3,6*2,26*3,6*2,26*3,6*2,26*3
  //   ,6*2,26*3,6*2,26*3,6*2,26*3,6*2,26*3,6*2,26*3,6*2,26*3,6*2,26*3
  //   ,6*2,26*3,6*2,26*3,6*2,26*3,6*2,26*3,6*2,26*3,6*2,26*3,6*2,26*3
  //   ,6*2,26*3,6*2,26*3,7*0,25*1,7*0,25*1,7*0,25*1,7*0,25*1,7*0,25*1
  //   ,7*0,25*1,7*0,25*1,7*2,25*3,7*2,25*3,7*2,25*3,7*2,25*3,7*2,25*3
  //   ,7*2,25*3,7*2,25*3,7*2,25*3,7*2,25*3,7*2,25*3,7*2,25*3,7*2,25*3
  //   ,7*2,25*3,7*2,25*3,7*2,25*3,7*2,25*3,7*2,25*3,7*2,25*3,7*2,25*3
  //   ,7*2,25*3,7*2,25*3,7*2,25*3,7*2,25*3,7*2,25*3,7*2,25*3,8*0,24*1
  //   ,8*0,24*1,8*0,24*1,8*0,24*1,8*0,24*1,8*0,24*1,8*0,24*1,8*0,24*1
  //   ,8*2,24*3,8*2,24*3,8*2,24*3,8*2,24*3,8*2,24*3,8*2,24*3,8*2,24*3
  //   ,8*2,24*3,8*2,24*3,8*2,24*3,8*2,24*3,8*2,24*3,8*2,24*3,8*2,24*3
  //   ,8*2,24*3,8*2,24*3,8*2,24*3,8*2,24*3,8*2,24*3,8*2,24*3,8*2,24*3
  //   ,8*2,24*3,8*2,24*3,8*2,24*3,9*0,23*1,9*0,23*1,9*0,23*1,9*0,23*1
  //   ,9*0,23*1,9*0,23*1,9*0,23*1,9*0,23*1,9*0,23*1,9*2,23*3,9*2,23*3
  //   ,9*2,23*3,9*2,23*3,9*2,23*3,9*2,23*3,9*2,23*3,9*2,23*3,9*2,23*3
  //   ,9*2,23*3,9*2,23*3,9*2,23*3,9*2,23*3,9*2,23*3,9*2,23*3,9*2,23*3
  //   ,9*2,23*3,9*2,23*3,9*2,23*3,9*2,23*3,9*2,23*3,9*2,23*3,9*2,23*3
  //   ,10*0,22*1,10*0,22*1,10*0,22*1,10*0,22*1,10*0,22*1,10*0,22*1,10*0
  //   ,22*1,10*0,22*1,10*0,22*1,10*0,22*1,10*2,22*3,10*2,22*3,10*2,22*3
  //   ,10*2,22*3,10*2,22*3,10*2,22*3,10*2,22*3,10*2,22*3,10*2,22*3,10*2
  //   ,22*3,10*2,22*3,10*2,22*3,10*2,22*3,10*2,22*3,10*2,22*3,10*2,22*3
  //   ,10*2,22*3,10*2,22*3,10*2,22*3,10*2,22*3,10*2,22*3,10*2,22*3,11*0
  //   ,21*1,11*0,21*1,11*0,21*1,11*0,21*1,11*0,21*1,11*0,21*1,11*0,21*1
  //   ,11*0,21*1,11*0,21*1,11*0,21*1,11*0,21*1,11*2,21*3,11*2,21*3,11*2
  //   ,21*3,11*2,21*3,11*2,21*3,11*2,21*3,11*2,21*3,11*2,21*3,11*2,21*3
  //   ,11*2,21*3,11*2,21*3,11*2,21*3,11*2,21*3,11*2,21*3,11*2,21*3,11*2
  //   ,21*3,11*2,21*3,11*2,21*3,11*2,21*3,11*2,21*3,11*2,21*3,12*0,20*1
  //   ,12*0,20*1,12*0,20*1,12*0,20*1,12*0,20*1,12*0,20*1,12*0,20*1,12*0
  //   ,20*1,12*0,20*1,12*0,20*1,12*0,20*1,12*0,20*1,12*2,20*3,12*2,20*3
  //   ,12*2,20*3,12*2,20*3,12*2,20*3,12*2,20*3,12*2,20*3,12*2,20*3,12*2
  //   ,20*3,12*2,20*3,12*2,20*3,12*2,20*3,12*2,20*3,12*2,20*3,12*2,20*3
  //   ,12*2,20*3,12*2,20*3,12*2,20*3,12*2,20*3,12*2,20*3,13*0,19*1,13*0
  //   ,19*1,13*0,19*1,13*0,19*1,13*0,19*1,13*0,19*1,13*0,19*1,13*0,19*1
  //   ,13*0,19*1,13*0,19*1,13*0,19*1,13*0,19*1,13*0,19*1,13*2,19*3,13*2
  //   ,19*3,13*2,19*3,13*2,19*3,13*2,19*3,13*2,19*3,13*2,19*3,13*2,19*3
  //   ,13*2,19*3,13*2,19*3,13*2,19*3,13*2,19*3,13*2,19*3,13*2,19*3,13*2
  //   ,19*3,13*2,19*3,13*2,19*3,13*2,19*3,13*2,19*3,14*0,18*1,14*0,18*1
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  //   contents of E3 (hex, n*v repeats v):
  //   0,31*1,2,31*3,2,31*3,2,31*3,2,31*3,2,31*3,2,31*3,2,31*3,2,31*3
  //   ,2,31*3,2,31*3,2,31*3,2,31*3,2,31*3,2,31*3,2,31*3,2,31*3,2,31*3
  //   ,2,31*3,2,31*3,2,31*3,2,31*3,2,31*3,2,31*3,2,31*3,2,31*3,2,31*3
  //   ,2,31*3,2,31*3,2,31*3,2,31*3,2,31*3,0,0,30*1,0,0,30*1,2,2,30*3
  //   ,2,2,30*3,2,2,30*3,2,2,30*3,2,2,30*3,2,2,30*3,2,2,30*3,2,2,30*3
  //   ,2,2,30*3,2,2,30*3,2,2,30*3,2,2,30*3,2,2,30*3,2,2,30*3,2,2,30*3
  //   ,2,2,30*3,2,2,30*3,2,2,30*3,2,2,30*3,2,2,30*3,2,2,30*3,2,2,30*3
  //   ,2,2,30*3,2,2,30*3,2,2,30*3,2,2,30*3,2,2,30*3,2,2,30*3,2,2,30*3
  //   ,2,2,30*3,0,0,0,29*1,0,0,0,29*1,0,0,0,29*1,2,2,2,29*3,2,2,2,29*3
  //   ,2,2,2,29*3,2,2,2,29*3,2,2,2,29*3,2,2,2,29*3,2,2,2,29*3,2,2,2
  //   ,29*3,2,2,2,29*3,2,2,2,29*3,2,2,2,29*3,2,2,2,29*3,2,2,2,29*3,2,2,2
  //   ,29*3,2,2,2,29*3,2,2,2,29*3,2,2,2,29*3,2,2,2,29*3,2,2,2,29*3,2,2,2
  //   ,29*3,2,2,2,29*3,2,2,2,29*3,2,2,2,29*3,2,2,2,29*3,2,2,2,29*3,2,2,2
  //   ,29*3,2,2,2,29*3,2,2,2,29*3,2,2,2,29*3,4*0,28*1,4*0,28*1,4*0,28*1
  //   ,4*0,28*1,4*2,28*3,4*2,28*3,4*2,28*3,4*2,28*3,4*2,28*3,4*2,28*3
  //   ,4*2,28*3,4*2,28*3,4*2,28*3,4*2,28*3,4*2,28*3,4*2,28*3,4*2,28*3
  //   ,4*2,28*3,4*2,28*3,4*2,28*3,4*2,28*3,4*2,28*3,4*2,28*3,4*2,28*3
  //   ,4*2,28*3,4*2,28*3,4*2,28*3,4*2,28*3,4*2,28*3,4*2,28*3,4*2,28*3
  //   ,4*2,28*3,5*0,27*1,5*0,27*1,5*0,27*1,5*0,27*1,5*0,27*1,5*2,27*3
  //   ,5*2,27*3,5*2,27*3,5*2,27*3,5*2,27*3,5*2,27*3,5*2,27*3,5*2,27*3
  //   ,5*2,27*3,5*2,27*3,5*2,27*3,5*2,27*3,5*2,27*3,5*2,27*3,5*2,27*3
  //   ,5*2,27*3,5*2,27*3,5*2,27*3,5*2,27*3,5*2,27*3,5*2,27*3,5*2,27*3
  //   ,5*2,27*3,5*2,27*3,5*2,27*3,5*2,27*3,5*2,27*3,6*0,26*1,6*0,26*1
  //   ,6*0,26*1,6*0,26*1,6*0,26*1,6*0,26*1,6*2,26*3,6*2,26*3,6*2,26*3
  //   ,6*2,26*3,6*2,26*3,6*2,26*3,6*2,26*3,6*2,26*3,6*2,26*3,6*2,26*3
  //   ,6*2,26*3,6*2,26*3,6*2,26*3,6*2,26*3,6*2,26*3,6*2,26*3,6*2,26*3
  //   ,6*2,26*3,6*2,26*3,6*2,26*3,6*2,26*3,6*2,26*3,6*2,26*3,6*2,26*3
  //   ,6*2,26*3,6*2,26*3,7*0,25*1,7*0,25*1,7*0,25*1,7*0,25*1,7*0,25*1
  //   ,7*0,25*1,7*0,25*1,7*2,25*3,7*2,25*3,7*2,25*3,7*2,25*3,7*2,25*3
  //   ,7*2,25*3,7*2,25*3,7*2,25*3,7*2,25*3,7*2,25*3,7*2,25*3,7*2,25*3
  //   ,7*2,25*3,7*2,25*3,7*2,25*3,7*2,25*3,7*2,25*3,7*2,25*3,7*2,25*3
  //   ,7*2,25*3,7*2,25*3,7*2,25*3,7*2,25*3,7*2,25*3,7*2,25*3,8*0,24*1
  //   ,8*0,24*1,8*0,24*1,8*0,24*1,8*0,24*1,8*0,24*1,8*0,24*1,8*0,24*1
  //   ,8*2,24*3,8*2,24*3,8*2,24*3,8*2,24*3,8*2,24*3,8*2,24*3,8*2,24*3
  //   ,8*2,24*3,8*2,24*3,8*2,24*3,8*2,24*3,8*2,24*3,8*2,24*3,8*2,24*3
  //   ,8*2,24*3,8*2,24*3,8*2,24*3,8*2,24*3,8*2,24*3,8*2,24*3,8*2,24*3
  //   ,8*2,24*3,8*2,24*3,8*2,24*3,9*0,23*1,9*0,23*1,9*0,23*1,9*0,23*1
  //   ,9*0,23*1,9*0,23*1,9*0,23*1,9*0,23*1,9*0,23*1,9*2,23*3,9*2,23*3
  //   ,9*2,23*3,9*2,23*3,9*2,23*3,9*2,23*3,9*2,23*3,9*2,23*3,9*2,23*3
  //   ,9*2,23*3,9*2,23*3,9*2,23*3,9*2,23*3,9*2,23*3,9*2,23*3,9*2,23*3
  //   ,9*2,23*3,9*2,23*3,9*2,23*3,9*2,23*3,9*2,23*3,9*2,23*3,9*2,23*3
  //   ,10*0,22*1,10*0,22*1,10*0,22*1,10*0,22*1,10*0,22*1,10*0,22*1,10*0
  //   ,22*1,10*0,22*1,10*0,22*1,10*0,22*1,10*2,22*3,10*2,22*3,10*2,22*3
  //   ,10*2,22*3,10*2,22*3,10*2,22*3,10*2,22*3,10*2,22*3,10*2,22*3,10*2
  //   ,22*3,10*2,22*3,10*2,22*3,10*2,22*3,10*2,22*3,10*2,22*3,10*2,22*3
  //   ,10*2,22*3,10*2,22*3,10*2,22*3,10*2,22*3,10*2,22*3,10*2,22*3,11*0
  //   ,21*1,11*0,21*1,11*0,21*1,11*0,21*1,11*0,21*1,11*0,21*1,11*0,21*1
  //   ,11*0,21*1,11*0,21*1,11*0,21*1,11*0,21*1,11*2,21*3,11*2,21*3,11*2
  //   ,21*3,11*2,21*3,11*2,21*3,11*2,21*3,11*2,21*3,11*2,21*3,11*2,21*3
  //   ,11*2,21*3,11*2,21*3,11*2,21*3,11*2,21*3,11*2,21*3,11*2,21*3,11*2
  //   ,21*3,11*2,21*3,11*2,21*3,11*2,21*3,11*2,21*3,11*2,21*3,12*0,20*1
  //   ,12*0,20*1,12*0,20*1,12*0,20*1,12*0,20*1,12*0,20*1,12*0,20*1,12*0
  //   ,20*1,12*0,20*1,12*0,20*1,12*0,20*1,12*0,20*1,12*2,20*3,12*2,20*3
  //   ,12*2,20*3,12*2,20*3,12*2,20*3,12*2,20*3,12*2,20*3,12*2,20*3,12*2
  //   ,20*3,12*2,20*3,12*2,20*3,12*2,20*3,12*2,20*3,12*2,20*3,12*2,20*3
  //   ,12*2,20*3,12*2,20*3,12*2,20*3,12*2,20*3,12*2,20*3,13*0,19*1,13*0
  //   ,19*1,13*0,19*1,13*0,19*1,13*0,19*1,13*0,19*1,13*0,19*1,13*0,19*1
  //   ,13*0,19*1,13*0,19*1,13*0,19*1,13*0,19*1,13*0,19*1,13*2,19*3,13*2
  //   ,19*3,13*2,19*3,13*2,19*3,13*2,19*3,13*2,19*3,13*2,19*3,13*2,19*3
  //   ,13*2,19*3,13*2,19*3,13*2,19*3,13*2,19*3,13*2,19*3,13*2,19*3,13*2
  //   ,19*3,13*2,19*3,13*2,19*3,13*2,19*3,13*2,19*3,14*0,18*1,14*0,18*1
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  //   contents of E1 (hex, n*v repeats v):
  //   C:\Users\gusbr\Desktop\CodingShit\Romulus-I\Specifications\Flash\rom_files\RGB.ROM false
  //   contents of E2 (hex, n*v repeats v):
  //   C:\Users\gusbr\Desktop\CodingShit\Romulus-I\Specifications\Flash\rom_files\RGB.ROM false
  //   contents of E3 (hex, n*v repeats v):
  //   C:\Users\gusbr\Desktop\CodingShit\Romulus-I\Specifications\Flash\rom_files\RGB.ROM false
endmodule
